# Fritzing sketch fotorezistor (saved by Fritzing 0.9.5d)
breadboards: 1

parts:
  A0 = female pin header, 1 pin [form="♀ (female)"]
  +5V = female pin header, 1 pin [form="♀ (female)"]
  R11 = Resistor [tolerance=±5% resistance=10k package=THT]
  Fotorezistor = Photocell (LDR) [package=THT]

nets:
  N1: A0.pin1, R11.Pin_1, Fotorezistor.pin_1
  N2: +5V.pin1, Fotorezistor.pin_0
  GND: R11.Pin_0
