# Fritzing sketch ledky (saved by Fritzing 0.9.5d)

parts:
  PIN_4 = female pin header, 1 pin [form="♀ (female)"]
  PIN_5 = female pin header, 1 pin [form="♀ (female)"]
  PIN_6 = female pin header, 1 pin [form="♀ (female)"]
  PIN_7 = female pin header, 1 pin [form="♀ (female)"]
  PIN_3 = female pin header, 1 pin [form="♀ (female)"]
  R1 = Resistor [tolerance=±5% resistance=220 package=THT]
  R2 = Resistor [tolerance=±5% resistance=220 package=THT]
  R3 = Resistor [tolerance=±5% resistance=220 package=THT]
  R4 = Resistor [tolerance=±5% resistance=220 package=THT]
  R5 = Resistor [tolerance=±5% resistance=220 package=THT]
  LED1 = LED - 5mm [color="White (8000K)" package="5 mm [THT]"]
  LED2 = LED - 5mm [color="Blue (505nm)" package="5 mm [THT]"]
  LED4 = LED - 5mm [color="Orange (612nm)" package="5 mm [THT]"]
  LED5 = LED - 5mm [color="Red (633nm)" package="5 mm [THT]"]
  LED3 = LED - 5mm [color="Green (565nm)" package="5 mm [THT]"]

nets:
  N1: PIN_4.pin1, R2.Pin_1
  N2: PIN_5.pin1, R3.Pin_1
  N3: PIN_6.pin1, R4.Pin_1
  N4: PIN_7.pin1, R5.Pin_1
  N5: PIN_3.pin1, R1.Pin_1
  N6: R1.Pin_0, LED1.anode
  N7: R2.Pin_0, LED2.anode
  N8: R3.Pin_0, LED3.anode
  N9: R4.Pin_0, LED4.anode
  N10: R5.Pin_0, LED5.anode
  GND: LED1.cathode, LED2.cathode, LED4.cathode, LED5.cathode, LED3.cathode
