# Fritzing sketch rgb (saved by Fritzing 0.9.5d)
breadboards: 1

parts:
  PIN_11 = female pin header, 1 pin [form="♀ (female)"]
  PIN_10 = female pin header, 1 pin [form="♀ (female)"]
  PIN_9 = female pin header, 1 pin [form="♀ (female)"]
  R8 = Resistor [tolerance=±5% resistance=220 package=THT]
  R6 = Resistor [tolerance=±5% resistance=220 package=THT]
  R7 = Resistor [tolerance=±5% resistance=220 package=THT]
  RGB_LED = RGB LED (com. cathode, rgb) [package="5 mm [THT]"]

nets:
  N1: PIN_11.pin1, R8.Pin_1
  N2: PIN_10.pin1, R7.Pin_1
  N3: PIN_9.pin1, R6.Pin_1
  N4: R8.Pin_0, RGB_LED.blue_anode
  N5: R6.Pin_0, RGB_LED.red_anode
  N6: R7.Pin_0, RGB_LED.green_anode
  GND: RGB_LED.common_cathode
