# Fritzing sketch tlacitko (saved by Fritzing 0.9.5d)
breadboards: 1

parts:
  PIN_2 = female pin header, 1 pin [form="♀ (female)"]
  R9 = Resistor [tolerance=±5% resistance=10k package=THT]
  +5V = female pin header, 1 pin [form="♀ (female)"]
  S1 = Pushbutton [package=THT]

nets:
  N1: PIN_2.pin1, R9.Pin_1, S1.leg0
  N2: R9.Pin_0, +5V.pin1
  GND: S1.leg1
